// Logisim project MeioSomadorAula02.circ as structural Verilog
module MeioSomador (
  input  A,
  input  B,
  output S,
  output Cout
);

  xor xor_1 (S, A, B);
  and and_1 (Cout, A, B);
endmodule

module SomadorCompleto (
  input  A,
  input  B,
  input  Cin,
  output S,
  output Cout
);

  wire meiosomador_1_cout, meiosomador_1_s, meiosomador_2_cout;

  MeioSomador meiosomador_1 (.Cout(meiosomador_1_cout), .S(meiosomador_1_s), .B(B), .A(A));
  MeioSomador meiosomador_2 (.Cout(meiosomador_2_cout), .S(S), .B(Cin), .A(meiosomador_1_s));
  or or_1 (Cout, meiosomador_1_cout, meiosomador_2_cout);
endmodule

module Somador_4Bits (
  input  [3:0] A,
  input  [3:0] B,
  output [3:0] out_3
);

  wire somadorcompleto_1_cout, somadorcompleto_2_cout, somadorcompleto_3_cout, somadorcompleto_4_cout;

  SomadorCompleto somadorcompleto_1 (
    .Cout(somadorcompleto_1_cout), .S(out_3[3]), .Cin(somadorcompleto_2_cout), .B(B[3]), .A(A[3]));
  SomadorCompleto somadorcompleto_2 (
    .Cout(somadorcompleto_2_cout), .S(out_3[2]), .Cin(somadorcompleto_3_cout), .B(B[2]), .A(A[2]));
  Hex_Digit_Display hex_digit_display_1 (.value(out_3));  // open: dp
  SomadorCompleto somadorcompleto_3 (
    .Cout(somadorcompleto_3_cout), .S(out_3[1]), .Cin(somadorcompleto_4_cout), .B(B[1]), .A(A[1]));
  SomadorCompleto somadorcompleto_4 (.Cout(somadorcompleto_4_cout), .S(out_3[0]), .Cin(1'b0), .B(B[0]), .A(A[0]));
  // also tied to GND on the sheet: somadorcompleto_1_cout
endmodule
