// Logisim project MeioSomadorSubtrator.circ as structural Verilog
module MeioSomador (
  input  A,
  input  B,
  output S,
  output Cout
);

  xor xor_1 (S, A, B);
  and and_1 (Cout, A, B);
endmodule

module SomadorCompleto (
  input  A,
  input  B,
  input  Cin,
  output S,
  output Cout
);

  wire meiosomador_1_cout, meiosomador_1_s, meiosomador_2_cout;

  MeioSomador meiosomador_1 (.Cout(meiosomador_1_cout), .B(B), .S(meiosomador_1_s), .A(A));
  MeioSomador meiosomador_2 (.Cout(meiosomador_2_cout), .B(Cin), .S(S), .A(meiosomador_1_s));
  or or_1 (Cout, meiosomador_1_cout, meiosomador_2_cout);
endmodule

module Somador_4Bits (
  input  [3:0] A,
  input  [3:0] B,
  output [3:0] out_3
);

  wire somadorcompleto_1_cout, somadorcompleto_2_cout, somadorcompleto_3_cout, somadorcompleto_4_cout;

  SomadorCompleto somadorcompleto_1 (
    .S(out_3[3]), .B(B[3]), .Cin(somadorcompleto_2_cout), .Cout(somadorcompleto_1_cout), .A(A[3]));
  SomadorCompleto somadorcompleto_2 (
    .S(out_3[2]), .B(B[2]), .Cin(somadorcompleto_3_cout), .Cout(somadorcompleto_2_cout), .A(A[2]));
  Hex_Digit_Display hex_digit_display_1 (.value(out_3));  // open: dp
  SomadorCompleto somadorcompleto_3 (
    .S(out_3[1]), .B(B[1]), .Cin(somadorcompleto_4_cout), .Cout(somadorcompleto_3_cout), .A(A[1]));
  SomadorCompleto somadorcompleto_4 (.S(out_3[0]), .B(B[0]), .Cin(1'b0), .Cout(somadorcompleto_4_cout), .A(A[0]));
  // also tied to GND on the sheet: somadorcompleto_1_cout
endmodule

module MeioSubtrator (
  input  A,
  input  B,
  output S,
  output Tout
);

  xor xor_1 (S, A, B);
  and and_1 (Tout, ~A, B);  // AND_Gate
endmodule

module SubtratorCompleto (
  input  A,
  input  B,
  input  Cin,
  output S,
  output Cout
);

  wire meiosubtrator_1_s, meiosubtrator_1_tout, meiosubtrator_2_tout;

  MeioSubtrator meiosubtrator_1 (.Tout(meiosubtrator_1_tout), .S(meiosubtrator_1_s), .B(B), .A(A));
  MeioSubtrator meiosubtrator_2 (.Tout(meiosubtrator_2_tout), .S(S), .B(Cin), .A(meiosubtrator_1_s));
  or or_1 (Cout, meiosubtrator_2_tout, meiosubtrator_1_tout);
endmodule

module Ex1AdSub (
);

  Demultiplexer #(.enable("false")) demultiplexer_1 ();  // open: out0, out1, in, sel
  Multiplexer #(.enable("false")) multiplexer_1 ();  // open: in0, in1, out, sel
  MeioSomador meiosomador_1 ();  // open: Cout, B, S, A
  MeioSubtrator meiosubtrator_1 ();  // open: Tout, S, B, A
endmodule
