// Logisim project NumerosSinalizados.circ as structural Verilog
module MeioSomador (
  input  A,
  input  B,
  output S,
  output Cout
);

  xor xor_1 (S, A, B);
  and and_1 (Cout, A, B);
endmodule

module SomadorCompleto (
  input  A,
  input  B,
  input  Cin,
  output S,
  output Cout
);

  wire meiosomador_1_cout, meiosomador_1_s, meiosomador_2_cout;

  MeioSomador meiosomador_1 (.Cout(meiosomador_1_cout), .S(meiosomador_1_s), .B(B), .A(A));
  MeioSomador meiosomador_2 (.Cout(meiosomador_2_cout), .S(S), .B(Cin), .A(meiosomador_1_s));
  or or_1 (Cout, meiosomador_1_cout, meiosomador_2_cout);
endmodule

module Somador_4Bits (
  input  [3:0] A,
  input  [3:0] B,
  output [3:0] out_3
);

  wire somadorcompleto_1_cout, somadorcompleto_2_cout, somadorcompleto_3_cout, somadorcompleto_4_cout;

  SomadorCompleto somadorcompleto_1 (
    .B(B[3]), .Cout(somadorcompleto_1_cout), .Cin(somadorcompleto_2_cout), .S(out_3[3]), .A(A[3]));
  SomadorCompleto somadorcompleto_2 (
    .B(B[2]), .Cout(somadorcompleto_2_cout), .Cin(somadorcompleto_3_cout), .S(out_3[2]), .A(A[2]));
  Hex_Digit_Display hex_digit_display_1 (.value(out_3));  // open: dp
  SomadorCompleto somadorcompleto_3 (
    .B(B[1]), .Cout(somadorcompleto_3_cout), .Cin(somadorcompleto_4_cout), .S(out_3[1]), .A(A[1]));
  SomadorCompleto somadorcompleto_4 (.B(B[0]), .Cout(somadorcompleto_4_cout), .Cin(1'b0), .S(out_3[0]), .A(A[0]));
  // also tied to GND on the sheet: somadorcompleto_1_cout
endmodule

module MeioSubtrator (
  input  A,
  input  B,
  output S,
  output Tout
);

  xor xor_1 (S, A, B);
  and and_1 (Tout, ~A, B);  // AND_Gate
endmodule

module SubtratorCompleto (
  input  A,
  input  B,
  input  Cin,
  output S,
  output Cout
);

  wire meiosubtrator_1_s, meiosubtrator_1_tout, meiosubtrator_2_tout;

  MeioSubtrator meiosubtrator_1 (.Tout(meiosubtrator_1_tout), .B(B), .S(meiosubtrator_1_s), .A(A));
  MeioSubtrator meiosubtrator_2 (.Tout(meiosubtrator_2_tout), .B(Cin), .S(S), .A(meiosubtrator_1_s));
  or or_1 (Cout, meiosubtrator_2_tout, meiosubtrator_1_tout);
endmodule

module Ex1AdSub (
);

  Demultiplexer #(.enable("false")) demultiplexer_1 ();  // open: out0, out1, in, sel
  Multiplexer #(.enable("false")) multiplexer_1 ();  // open: in0, in1, out, sel
  MeioSomador meiosomador_1 ();  // open: Cout, S, B, A
  MeioSubtrator meiosubtrator_1 ();  // open: Tout, B, S, A
endmodule

module Complemento2 (
  input  [3:0] A,
  input  [3:0] B,
  input  Cin,
  output Cout,
  output [3:0] s
);

  wire multiplexer_1_out, multiplexer_2_out, multiplexer_3_out, multiplexer_4_out, not_1_out, not_2_out,
       not_3_out, not_4_out, somadorcompleto_2_cout, somadorcompleto_3_cout, somadorcompleto_4_cout;

  not not_1 (not_1_out, B[3]);
  Multiplexer #(.enable("false")) multiplexer_1 (.in0(B[3]), .in1(not_1_out), .out(multiplexer_1_out), .sel(Cin));
  SomadorCompleto somadorcompleto_1 (
    .B(multiplexer_1_out), .Cout(Cout), .Cin(somadorcompleto_2_cout), .S(s[3]), .A(A[3]));
  Multiplexer #(.enable("false")) multiplexer_2 (.in0(B[2]), .in1(not_2_out), .out(multiplexer_2_out), .sel(Cin));
  not not_2 (not_2_out, B[2]);
  SomadorCompleto somadorcompleto_2 (
    .B(multiplexer_2_out), .Cout(somadorcompleto_2_cout), .Cin(somadorcompleto_3_cout), .S(s[2]), .A(A[2]));
  not not_3 (not_3_out, B[1]);
  Multiplexer #(.enable("false")) multiplexer_3 (.in0(B[1]), .in1(not_3_out), .out(multiplexer_3_out), .sel(Cin));
  SomadorCompleto somadorcompleto_3 (
    .B(multiplexer_3_out), .Cout(somadorcompleto_3_cout), .Cin(somadorcompleto_4_cout), .S(s[1]), .A(A[1]));
  not not_4 (not_4_out, B[0]);
  Multiplexer #(.enable("false")) multiplexer_4 (.in0(B[0]), .in1(not_4_out), .out(multiplexer_4_out), .sel(Cin));
  SomadorCompleto somadorcompleto_4 (
    .B(multiplexer_4_out), .Cout(somadorcompleto_4_cout), .Cin(Cin), .S(s[0]), .A(A[0]));
endmodule

module Multiplicacao (
  input  A1,
  input  A0,
  input  B1,
  input  B0,
  output P3,
  output P2,
  output P1,
  output P0
);

  wire and_1_out, and_2_out, and_3_out, meiosomador_2_cout;

  and and_1 (and_1_out, A1, B1);
  MeioSomador meiosomador_1 (.Cout(P3), .S(P2), .B(and_1_out), .A(meiosomador_2_cout));
  and and_2 (and_2_out, A1, B0);
  and and_3 (and_3_out, A0, B1);
  MeioSomador meiosomador_2 (.Cout(meiosomador_2_cout), .S(P1), .B(and_2_out), .A(and_3_out));
  and and_4 (P0, A0, B0);
endmodule

module RegistradorDeDeslocamentoComCargaParalela (
  input  [3:0] D,
  input  [3:0] Q,
  input  Clock,
  input  Carga,
  input  Clear
);

  wire multiplexer_1_out, multiplexer_2_out, multiplexer_3_out, multiplexer_4_out;

  D_Flip_Flop d_ff_1 (.D(multiplexer_1_out), .clk(Clock), .Q(Q[0]), .reset(Clear));  // open: Qn, preset
  Multiplexer #(.enable("false")) multiplexer_1 (.in0(Q[0]), .in1(D[0]), .out(multiplexer_1_out), .sel(Carga));
  D_Flip_Flop d_ff_2 (.D(multiplexer_2_out), .clk(Clock), .Q(Q[1]), .reset(Clear));  // open: Qn, preset
  Multiplexer #(.enable("false")) multiplexer_2 (.in0(Q[1]), .in1(D[1]), .out(multiplexer_2_out), .sel(Carga));
  D_Flip_Flop d_ff_3 (.D(multiplexer_3_out), .clk(Clock), .Q(Q[2]), .reset(Clear));  // open: Qn, preset
  Multiplexer #(.enable("false")) multiplexer_3 (.in0(Q[2]), .in1(D[2]), .out(multiplexer_3_out), .sel(Carga));
  Multiplexer #(.enable("false")) multiplexer_4 (.in0(Q[3]), .in1(D[3]), .out(multiplexer_4_out), .sel(Carga));
  D_Flip_Flop d_ff_4 (.D(multiplexer_4_out), .clk(Clock), .Q(Q[3]), .reset(Clear));  // open: Qn, preset
endmodule
