// Logisim project projeto2_C208.circ as structural Verilog: 2 circuits, main circuit main
module main (
  input  [3:0] in_1
);

  wire ALU_SRC, CLK, LOAD, MEM_TO_REG, REG_DEST, REG_W, registerfile_1_p7, STORE;
  wire [4:0] multiplexer_1_out;
  wire [5:0] FUNCT;
  wire [31:0] adder_1_out, bit_extender_1_out, mips_alu_1_p4, mips_ram_1_p6, multiplexer_2_out, register_1_q,
       registerfile_1_p1, registerfile_1_p8;
  wire [31:6] mipsprogramrom_1_p2;

  Adder #(.width(32)) adder_1 (.a(register_1_q), .b(32'h4), .out(adder_1_out));  // open: cin, cout
  Register #(.width(32)) register_1 (.D(adder_1_out), .Q(register_1_q), .clk(CLK));  // open: en, clr
  Clock clock_1 (.out(CLK));
  // MIPSProgramROM mipsprogramrom_1: pin names not known; wires that end beside it: register_1_q, {mipsprogramrom_1_p2, FUNCT}
  Multiplexer #(.width(5)) multiplexer_1 (
    .in0(mipsprogramrom_1_p2[15:11]), .in1(mipsprogramrom_1_p2[20:16]), .out(multiplexer_1_out),
    .sel(REG_DEST));  // open: en
  assign bit_extender_1_out = {{16{1'b0}}, {mipsprogramrom_1_p2[15:6], FUNCT}};  // Bit_Extender bit_extender_1
  Unidade_de_Controle unidade_de_controle_1 (
    .OP_CODE(mipsprogramrom_1_p2[31:26]), .REG_DEST(REG_DEST), .REG_W(REG_W), .ALU_SRC(ALU_SRC),
    .FUNCT(FUNCT), .STORE(STORE), .LOAD(LOAD), .MEM_TO_REG(MEM_TO_REG));
  // RegisterFile registerfile_1: pin names not known; wires that end beside it: registerfile_1_p1, CLK, REG_W, multiplexer_1_out, mipsprogramrom_1_p2[25:21], mipsprogramrom_1_p2[20:16], registerfile_1_p7, registerfile_1_p8
  Multiplexer #(.width(32)) multiplexer_2 (
    .in0(registerfile_1_p8), .in1(bit_extender_1_out), .out(multiplexer_2_out), .sel(ALU_SRC));  // open: en
  // Mips_ALU mips_alu_1: pin names not known; wires that end beside it: registerfile_1_p7, multiplexer_2_out, in_1, mips_alu_1_p4
  // MIPS_RAM mips_ram_1: pin names not known; wires that end beside it: mips_alu_1_p4[19:0], registerfile_1_p8, STORE, CLK, LOAD, mips_ram_1_p6
  Multiplexer #(.width(32)) multiplexer_3 (
    .in0(mips_alu_1_p4), .in1(mips_ram_1_p6), .out(registerfile_1_p1), .sel(MEM_TO_REG));  // open: en

  // Notes on the sheet:
  //   MEMÓRIA DE PROGRAMA
  //   R
  //   I
  //   R
  //   I
endmodule

module Unidade_de_Controle (
  input  [5:0] OP_CODE,
  input  [5:0] FUNCT,
  output REG_DEST,
  output REG_W,
  output ALU_SRC,
  output STORE,
  output LOAD,
  output MEM_TO_REG
);

  wire ADDIU_out, and_1_out, FUNCT_NOR_out, NOR_out;

  and ADDIU (ADDIU_out, OP_CODE[0], ~OP_CODE[1], ~OP_CODE[2], OP_CODE[3], ~OP_CODE[4], ~OP_CODE[5]);  // AND_Gate
  and NOR (NOR_out, ~OP_CODE[0], ~OP_CODE[1], ~OP_CODE[2], ~OP_CODE[3], ~OP_CODE[4], ~OP_CODE[5]);  // AND_Gate
  and FUNCT_NOR (FUNCT_NOR_out, FUNCT[0], FUNCT[1], FUNCT[2], ~FUNCT[3], ~FUNCT[4], FUNCT[5]);  // AND_Gate
  and SW (STORE, OP_CODE[0], OP_CODE[1], ~OP_CODE[2], OP_CODE[3], ~OP_CODE[4], OP_CODE[5]);  // AND_Gate
  and LW (LOAD, OP_CODE[0], OP_CODE[1], ~OP_CODE[2], ~OP_CODE[3], ~OP_CODE[4], OP_CODE[5]);  // AND_Gate
  and and_1 (and_1_out, NOR_out, FUNCT_NOR_out);
  or or_1 (REG_DEST, ADDIU_out, STORE, LOAD);
  or or_2 (REG_W, ADDIU_out, and_1_out, LOAD);
  or or_3 (ALU_SRC, ADDIU_out, STORE, LOAD);

  assign MEM_TO_REG = LOAD;
endmodule
