// Logisim project Projeto_Alu.circ as structural Verilog
module MeioSomador (
  input  A,
  input  B,
  output S,
  output Cout
);

  xor xor_1 (S, A, B);
  and and_1 (Cout, A, B);
endmodule

module SomadorCompleto (
  input  A,
  input  B,
  input  Cin,
  output S,
  output Cout
);

  wire meiosomador_1_cout, meiosomador_1_s, meiosomador_2_cout;

  MeioSomador meiosomador_1 (.Cout(meiosomador_1_cout), .B(B), .S(meiosomador_1_s), .A(A));
  MeioSomador meiosomador_2 (.Cout(meiosomador_2_cout), .B(Cin), .S(S), .A(meiosomador_1_s));
  or or_1 (Cout, meiosomador_1_cout, meiosomador_2_cout);
endmodule

module MeioSubtrator (
  input  A,
  input  B,
  output S,
  output Tout
);

  xor xor_1 (S, A, B);
  and and_1 (Tout, ~A, B);  // AND_Gate
endmodule

module SubtratorCompleto (
  input  A,
  input  B,
  input  Cin,
  output S,
  output Cout
);

  wire meiosubtrator_1_s, meiosubtrator_1_tout, meiosubtrator_2_tout;

  MeioSubtrator meiosubtrator_1 (.Tout(meiosubtrator_1_tout), .S(meiosubtrator_1_s), .B(B), .A(A));
  MeioSubtrator meiosubtrator_2 (.Tout(meiosubtrator_2_tout), .S(S), .B(Cin), .A(meiosubtrator_1_s));
  or or_1 (Cout, meiosubtrator_2_tout, meiosubtrator_1_tout);
endmodule

module Somador_8Bits (
  input  [7:0] A,
  input  [7:0] B,
  output [7:0] S
);

  wire somadorcompleto_1_cout, somadorcompleto_2_cout, somadorcompleto_3_cout, somadorcompleto_4_cout,
       somadorcompleto_5_cout, somadorcompleto_6_cout, somadorcompleto_7_cout, somadorcompleto_8_cout;

  SomadorCompleto somadorcompleto_1 (
    .Cout(somadorcompleto_1_cout), .S(S[7]), .Cin(somadorcompleto_2_cout), .B(B[7]), .A(A[7]));
  SomadorCompleto somadorcompleto_2 (
    .Cout(somadorcompleto_2_cout), .S(S[6]), .Cin(somadorcompleto_3_cout), .B(B[6]), .A(A[6]));
  SomadorCompleto somadorcompleto_3 (
    .Cout(somadorcompleto_3_cout), .S(S[5]), .Cin(somadorcompleto_4_cout), .B(B[5]), .A(A[5]));
  SomadorCompleto somadorcompleto_4 (
    .Cout(somadorcompleto_4_cout), .S(S[4]), .Cin(somadorcompleto_5_cout), .B(B[4]), .A(A[4]));
  SomadorCompleto somadorcompleto_5 (
    .Cout(somadorcompleto_5_cout), .S(S[3]), .Cin(somadorcompleto_6_cout), .B(B[3]), .A(A[3]));
  SomadorCompleto somadorcompleto_6 (
    .Cout(somadorcompleto_6_cout), .S(S[2]), .Cin(somadorcompleto_7_cout), .B(B[2]), .A(A[2]));
  SomadorCompleto somadorcompleto_7 (
    .Cout(somadorcompleto_7_cout), .S(S[1]), .Cin(somadorcompleto_8_cout), .B(B[1]), .A(A[1]));
  SomadorCompleto somadorcompleto_8 (.Cout(somadorcompleto_8_cout), .S(S[0]), .Cin(1'b0), .B(B[0]), .A(A[0]));
  // also tied to GND on the sheet: somadorcompleto_1_cout
endmodule

module Subtrator_8Bits (
  input  [7:0] A,
  input  [7:0] B,
  output [7:0] S
);

  wire subtratorcompleto_1_cout, subtratorcompleto_2_cout, subtratorcompleto_3_cout,
       subtratorcompleto_4_cout, subtratorcompleto_5_cout, subtratorcompleto_6_cout,
       subtratorcompleto_7_cout, subtratorcompleto_8_cout;

  SubtratorCompleto subtratorcompleto_1 (
    .B(B[7]), .Cout(subtratorcompleto_1_cout), .Cin(subtratorcompleto_2_cout), .S(S[7]), .A(A[7]));
  SubtratorCompleto subtratorcompleto_2 (
    .B(B[6]), .Cout(subtratorcompleto_2_cout), .Cin(subtratorcompleto_3_cout), .S(S[6]), .A(A[6]));
  SubtratorCompleto subtratorcompleto_3 (
    .B(B[5]), .Cout(subtratorcompleto_3_cout), .Cin(subtratorcompleto_4_cout), .S(S[5]), .A(A[5]));
  SubtratorCompleto subtratorcompleto_4 (
    .B(B[4]), .Cout(subtratorcompleto_4_cout), .Cin(subtratorcompleto_5_cout), .S(S[4]), .A(A[4]));
  SubtratorCompleto subtratorcompleto_5 (
    .B(B[3]), .Cout(subtratorcompleto_5_cout), .Cin(subtratorcompleto_6_cout), .S(S[3]), .A(A[3]));
  SubtratorCompleto subtratorcompleto_6 (
    .B(B[2]), .Cout(subtratorcompleto_6_cout), .Cin(subtratorcompleto_7_cout), .S(S[2]), .A(A[2]));
  SubtratorCompleto subtratorcompleto_7 (
    .B(B[1]), .Cout(subtratorcompleto_7_cout), .Cin(subtratorcompleto_8_cout), .S(S[1]), .A(A[1]));
  SubtratorCompleto subtratorcompleto_8 (.B(B[0]), .Cout(subtratorcompleto_8_cout), .Cin(1'b0), .S(S[0]), .A(A[0]));
  // also tied to GND on the sheet: subtratorcompleto_1_cout
endmodule

module Projeto_ALU (
  input  [7:0] A,
  input  [7:0] B,
  input  [2:0] D1,
  input  [3:0] OP,
  input  [2:0] D2,
  output [7:0] S
);

  wire [7:0] and_1_out, multiplier_1_out, nand_1_out, nor_1_out, not_1_out, or_1_out, shifter_1_out,
       shifter_2_out, somador_8bits_1_s, subtrator_8bits_1_s, xnor_1_out, xor_1_out;

  Multiplier multiplier_1 (.a(A), .b(B), .out(multiplier_1_out));  // open: cin, cout
  Shifter #(.shift("lr")) shifter_1 (.in(A), .\dist (D1), .out(shifter_1_out));
  assign nand_1_out = ~(A & B);  // NAND_Gate nand_1, 8 bits wide
  assign not_1_out = ~A;  // NOT_Gate not_1, 8 bits wide
  assign or_1_out = A | B;  // OR_Gate or_1, 8 bits wide
  assign xnor_1_out = ~(A ^ B);  // XNOR_Gate xnor_1, 8 bits wide
  Shifter shifter_2 (.in(A), .\dist (D2), .out(shifter_2_out));
  assign xor_1_out = A ^ B;  // XOR_Gate xor_1, 8 bits wide
  assign and_1_out = A & B;  // AND_Gate and_1, 8 bits wide
  assign nor_1_out = ~(A | B);  // NOR_Gate nor_1, 8 bits wide
  Subtrator_8Bits subtrator_8bits_1 (.A(A), .B(B), .S(subtrator_8bits_1_s));
  Somador_8Bits somador_8bits_1 (.A(A), .B(B), .S(somador_8bits_1_s));
  Multiplexer #(.select(4), .width(8), .enable("false")) multiplexer_1 (
    .in0({8{1'b0}}), .in1(subtrator_8bits_1_s), .in2(multiplier_1_out), .in3({8{1'b0}}), .in4(shifter_1_out),
    .in5(nand_1_out), .in6({8{1'b0}}), .in7(somador_8bits_1_s), .in8(not_1_out), .in9(or_1_out),
    .in10(xnor_1_out), .in11(shifter_2_out), .in12(xor_1_out), .in13({8{1'b0}}), .in14(and_1_out),
    .in15(nor_1_out), .out(S), .sel(OP));
endmodule
